# Fritzing sketch MicroProFightStickSchematicBreadboard (saved by Fritzing 0.9.3b)
breadboards: 1

parts:
  Part1 = Arduino Pro Micro (Clone)
  BUTTON1 = Arcade Button (red)
  BUTTON2 = Arcade Button (red)
  BUTTON3 = Arcade Button (red)
  BUTTON4 = Arcade Button (red)
  BUTTON5 = Arcade Button (red)
  BUTTON7 = Arcade Button (red)
  BUTTON8 = Arcade Button (red)
  BUTTON9 = Arcade Button (red)
  BUTTON10 = Arcade Button (red)
  BUTTON11 = Arcade Button (red)
  BUTTON12 = Arcade Button (red)
  BUTTON13 = Arcade Button (red)
  BUTTON14 = Arcade Button (red)
  BUTTON15 = Arcade Button (red)

nets:
  N1: Part1.TXO, BUTTON1.no_name_yet#2
  N2: Part1.RXI, BUTTON2.no_name_yet#2
  N3: Part1.GND, BUTTON1.no_name_yet#1, BUTTON2.no_name_yet#1, BUTTON3.no_name_yet#1, BUTTON4.no_name_yet#1, BUTTON5.no_name_yet#1, BUTTON7.no_name_yet#1, BUTTON8.no_name_yet#1, BUTTON9.no_name_yet#1, BUTTON10.no_name_yet#1, BUTTON11.no_name_yet#1, BUTTON12.no_name_yet#2, BUTTON13.no_name_yet#2, BUTTON14.no_name_yet#2, BUTTON15.no_name_yet#2
  N4: Part1.D2, BUTTON3.no_name_yet#2
  N5: Part1.D3, BUTTON4.no_name_yet#2
  N6: Part1.D4, BUTTON5.no_name_yet#2
  N7: Part1.D5, BUTTON7.no_name_yet#2
  N8: Part1.D6, BUTTON8.no_name_yet#2
  N9: Part1.D7, BUTTON9.no_name_yet#2
  N10: Part1.D8, BUTTON10.no_name_yet#2
  N11: Part1.D9, BUTTON11.no_name_yet#2
  N12: Part1.D10, BUTTON15.no_name_yet#1
  N13: Part1.D14, BUTTON13.no_name_yet#1
  N14: Part1.D15, BUTTON12.no_name_yet#1

custom parts:
  Arcade Button (red): Adafruit Arcade Button (red)
